// Logisim project PipelinedMips.circ as structural Verilog: 18 circuits, main circuit main
module main (
  input  memReset,
  output [9:0] misses,
  output [9:0] Cache_accesses,
  output [9:0] RAM_accesses,
  output miss
);

  wire ALUSrc, Branch, clock, ex_mem_1_alu0_2, ex_mem_1_alu1_2, ex_mem_1_alu2_2, ex_mem_1_alusrc_2,
       ex_mem_1_bracnh_2, ex_mem_1_jal_2, ex_mem_1_jr_2, ex_mem_1_jump_2, ex_mem_1_memtoreg_2,
       ex_mem_1_regdest_2, EX_MEM_RegWrite, hazard_detect_1_stalling_now, ID_EX_MemRead, IF_ID_Write, jal,
       Jr, Jump, MemForward, MemRead, MemToReg, MemWrite, MemWrite_Dec, or_2_out, PC_Write, PCSrc, RegDest,
       RegWrite, rg_ex_1_memtoreg_2, rg_ex_1_memwrite_2, rg_ex_1_regwrote_2, Squish, Squish_Fetch,
       Stall_Control, Zero, ZeroR;
  wire [1:0] FA, FB;
  wire [2:0] ALUctrl;
  wire [4:0] EX_MEM_RD, ID_EX_Rt, multiplexer_4_out, multiplexer_7_out, rg_ex_1__11_15_2, Rs, shmt, WrADDr;
  wire [5:0] Bit0_5, Bit26_31;
  wire [12:0] control_unit_1_p13, multiplexer_2_out;
  wire [15:6] Bit0_15;
  wire [25:0] Bit0_25_Ex;
  wire [25:16] Bit0_25;
  wire [31:0] A, A_Forw_EX, ALU, alu_1_aluresult, ALUR, B, Data, ex_mem_2_alu_2, ex_mem_2_pc_2, extend,
       Jal_value, Mem_Data, multiplexer_1_out, multiplexer_6_out, multiplexer_8_out, multiplexer_11_out, PC,
       PC4, PC_in, PC_l1, PC_L2, PC_plus, RD, RD1, RD2, rom_1_data, shift_left2_1_p2, signextend_1_p2,
       subtractor_1_out, WrData;

  Clock clock_1 (.out(clock));
  // Probe on A_Forw_EX
  // Probe on multiplexer_1_out
  Multiplexer #(.width(32), .enable("false")) multiplexer_1 (
    .in0(PC_in), .in1(A_Forw_EX), .out(multiplexer_1_out), .sel(Jr));
  Register #(.width(32)) u_PC (.D(multiplexer_1_out), .en(PC_Write), .Q(PC), .clk(clock));  // open: clr
  or or_1 (Squish, Jump, PCSrc, Jr);
  // Probe on PC
  Adder #(.width(32)) adder_1 (.a(PC), .b(32'h4), .out(PC4));  // open: cin, cout
  ROM #(.dataWidth(32)) rom_1 (.addr(PC[9:2]), .data(rom_1_data));  // open: sel
  IF_D if_d_1 (
    .PC(rom_1_data), .PC_plus(PC4), .IR({Bit26_31, Bit0_25, Bit0_15, Bit0_5}), .PC_plus_2(PC_plus),
    .Clock(clock), .NotStall(IF_ID_Write), .Squish(Squish), .Squish_2(Squish_Fetch));
  // Probe on {Bit26_31, Bit0_25, Bit0_15, Bit0_5}
  // Probe on WrData
  // Probe on WrADDr
  RegFile regfile_1 (
    .WrAddr(WrADDr), .WrData(WrData), .WrReg(RegWrite), .RdAddr1(Bit0_25[25:21]), .RdAddr2(Bit0_25[20:16]),
    .RdData1(RD1), .RdData2(RD2), .Clock(clock));
  // SingleCycle_Control_Unit control_unit_1: pin names not known; wires that end beside it: Bit26_31[5], Bit26_31[4], Bit26_31[3], Bit26_31[2], Bit26_31[1], Bit26_31[0], Bit0_5[5], Bit0_5[4], Bit0_5[3], Bit0_5[2], Bit0_5[1], Bit0_5[0], control_unit_1_p13[0], control_unit_1_p13[1], control_unit_1_p13[2], control_unit_1_p13[3], control_unit_1_p13[4], control_unit_1_p13[5], control_unit_1_p13[6], control_unit_1_p13[7], MemWrite_Dec, control_unit_1_p13[9], control_unit_1_p13[10], control_unit_1_p13[11], control_unit_1_p13[12], {control_unit_1_p13[12:9], MemWrite_Dec, control_unit_1_p13[7:0]}
  Hazard_Detect hazard_detect_1 (
    .ID_EX_MemRead(ID_EX_MemRead), .ID_EX_Rt(ID_EX_Rt), .IF_ID_Rs(Bit0_25[25:21]), .IF_ID_Rt(Bit0_25[20:16]),
    .IF_ID_Write(IF_ID_Write), .PC_Write(PC_Write), .Stall_Control(Stall_Control),
    .Stalling_Now(hazard_detect_1_stalling_now), .LW_Instruction(MemWrite_Dec));
  // Probe on RD1
  // Probe on hazard_detect_1_stalling_now
  // Probe on RD2
  or or_2 (or_2_out, Squish, Squish_Fetch, Stall_Control);
  Multiplexer #(.width(13), .enable("false")) multiplexer_2 (
    .in0({control_unit_1_p13[12:9], MemWrite_Dec, control_unit_1_p13[7:0]}), .in1({13{1'b0}}),
    .out(multiplexer_2_out), .sel(or_2_out));
  // Probe on {Bit0_15, Bit0_5}
  // Probe on signextend_1_p2
  // SingleCycle_SignExtend signextend_1: pin names not known; wires that end beside it: {Bit0_15, Bit0_5}, signextend_1_p2
  // Probe on Jal_value
  Multiplexer #(.select(2), .width(32)) multiplexer_3 (
    .in0(B), .in1(WrData), .in2(ALUR), .out(RD), .sel(FB));  // open: in3, en
  RG_EX rg_ex_1 (
    .ALU2(multiplexer_2_out[0]), .ALU1(multiplexer_2_out[1]), .ALU0(multiplexer_2_out[2]),
    .RegDest(multiplexer_2_out[3]), .Jump(multiplexer_2_out[4]), .Bracnh(multiplexer_2_out[5]),
    .MemRead(multiplexer_2_out[6]), .MemtoReg(multiplexer_2_out[7]), .MemWrite(multiplexer_2_out[8]),
    .ALUSrc(multiplexer_2_out[9]), .RegWrote(multiplexer_2_out[10]), .Jr(multiplexer_2_out[11]),
    .Jal(multiplexer_2_out[12]), .pc(PC_plus), .ALU2_2(ALUctrl[2]), .ALU0_2(ALUctrl[0]), .Jump_2(Jump),
    .MemRead_2(ID_EX_MemRead), .MemWrite_2(rg_ex_1_memwrite_2), .RegWrote_2(rg_ex_1_regwrote_2),
    .ALU1_2(ALUctrl[1]), .RegDest_2(RegDest), .Bracnh_2(Branch), .ALUSrc_2(ALUSrc), .Jr_2(Jr),
    .MemtoReg_2(rg_ex_1_memtoreg_2), .Jal_2(jal), .pc_2(Jal_value), .RD1(RD1), .RD2(RD2),
    .Exted(signextend_1_p2), .RD1_2(A), .RD2_2(B), .Exted_2(extend), ._16_20(Bit0_25[20:16]), .Clock(clock),
    ._11_15(Bit0_15[15:11]), ._16_20_2(ID_EX_Rt), ._11_15_2(rg_ex_1__11_15_2), .SHIFT(Bit0_15[10:6]),
    .SHIFT_2(shmt), .Stall(1'b1), ._21_25(Bit0_25[25:21]), ._21_25_2(Rs),
    .Bit_0_25({Bit0_25, Bit0_15, Bit0_5}), .Bit_0_25_2(Bit0_25_Ex));
  Subtractor #(.width(32)) subtractor_1 (.a(Jal_value), .b({32{1'b0}}), .out(subtractor_1_out));  // open: bin, bout
  Multiplexer #(.width(5)) multiplexer_4 (
    .in0(ID_EX_Rt), .in1(rg_ex_1__11_15_2), .out(multiplexer_4_out), .sel(RegDest));  // open: en
  // Probe on extend
  Multiplexer #(.select(2), .width(32)) multiplexer_5 (
    .in0(A), .in1(WrData), .in2(ALUR), .out(A_Forw_EX), .sel(FA));  // open: in3, en
  Multiplexer #(.width(32)) multiplexer_6 (.in0(RD), .in1(extend), .out(multiplexer_6_out), .sel(ALUSrc));  // open: en
  // Probe on extend
  Multiplexer #(.width(5), .enable("false")) multiplexer_7 (
    .in0(multiplexer_4_out), .in1({5{1'b1}}), .out(multiplexer_7_out), .sel(jal));
  // Probe on {subtractor_1_out[31:28], Bit0_25_Ex, 2'b00}
  // SingleCycle_Shift_Left2 shift_left2_1: pin names not known; wires that end beside it: extend, shift_left2_1_p2, PC_L2
  // Probe on shift_left2_1_p2
  // Probe on A_Forw_EX
  ALU alu_1 (
    .ALUCtl(ALUctrl), .A(A_Forw_EX), .B(multiplexer_6_out), .ALUResult(alu_1_aluresult), .Zero(Zero),
    .Shamt(shmt));  // open: Overflow
  // Probe on FA
  ForwardingUnit forwardingunit_1 (
    .ID_EX_RS(Rs), .ID_EX_RT(ID_EX_Rt), .EX_MEM_RegWrite(EX_MEM_RegWrite), .EX_MEM_RegRd(EX_MEM_RD),
    .MEM_WB_RegWrite(RegWrite), .MEM_WB_RegRd(WrADDr), .EX_MEM_MemWr(MemWrite), .ForwardA(FA), .ForwardB(FB),
    .MemForward(MemForward));
  Adder #(.width(32)) adder_2 (.a(Jal_value), .b(shift_left2_1_p2), .out(PC_l1));  // open: cin, cout
  EX_MEM ex_mem_1 (
    .ALU2(ALUctrl[2]), .ALU1(ALUctrl[1]), .ALU0(ALUctrl[0]), .RegDest(RegDest), .Jump(Jump), .Bracnh(Branch),
    .MemRead(ID_EX_MemRead), .MemtoReg(rg_ex_1_memtoreg_2), .MemWrite(rg_ex_1_memwrite_2), .ALUSrc(ALUSrc),
    .RegWrote(rg_ex_1_regwrote_2), .Jr(Jr), .Jal(jal), .pc(PC_l1), .ALU(ALU), .RD2(RD), .Zero(Zero),
    .ALU_2(ALUR), .RD2_2(Mem_Data), .Zero_2(ZeroR), .ALU2_2(ex_mem_1_alu2_2), .ALU0_2(ex_mem_1_alu0_2),
    .Jump_2(ex_mem_1_jump_2), .MemRead_2(MemRead), .MemWrite_2(MemWrite), .RegWrote_2(EX_MEM_RegWrite),
    .ALU1_2(ex_mem_1_alu1_2), .RegDest_2(ex_mem_1_regdest_2), .Bracnh_2(ex_mem_1_bracnh_2),
    .ALUSrc_2(ex_mem_1_alusrc_2), .Jr_2(ex_mem_1_jr_2), .MemtoReg_2(ex_mem_1_memtoreg_2),
    .Jal_2(ex_mem_1_jal_2), .pc_2(PC_L2), .dest(multiplexer_7_out), .dest_2(EX_MEM_RD), .clock(clock));
  Multiplexer #(.width(32), .enable("false")) multiplexer_8 (
    .in0(PC4), .in1(PC_l1), .out(multiplexer_8_out), .sel(PCSrc));
  Multiplexer #(.width(32), .enable("false")) multiplexer_9 (
    .in0(alu_1_aluresult), .in1(Jal_value), .out(ALU), .sel(jal));
  // Probe on FB
  Multiplexer #(.width(32), .enable("false")) multiplexer_10 (
    .in0(multiplexer_8_out), .in1({subtractor_1_out[31:28], Bit0_25_Ex, 2'b00}), .out(PC_in), .sel(Jump));
  // Probe on ALU
  // Probe on PC_in
  Multiplexer #(.width(32), .enable("false")) multiplexer_11 (
    .in0(Mem_Data), .in1(WrData), .out(multiplexer_11_out), .sel(MemForward));
  and and_1 (PCSrc, Branch, Zero);
  // Probe on multiplexer_11_out
  memory memory_1 (
    .addr(ALUR[7:0]), .data_in(multiplexer_11_out), .miss(miss), .misses(misses),
    .Cache_accesses(Cache_accesses), .RAM_accesses(RAM_accesses), .clock(clock), .reset(memReset),
    .memWrite(MemWrite), .memRead(MemRead), .data(Data));
  EX_MEM ex_mem_2 (
    .ALU2(ex_mem_1_alu2_2), .ALU1(ex_mem_1_alu1_2), .ALU0(ex_mem_1_alu0_2), .RegDest(ex_mem_1_regdest_2),
    .Jump(ex_mem_1_jump_2), .Bracnh(ex_mem_1_bracnh_2), .MemRead(MemRead), .MemtoReg(ex_mem_1_memtoreg_2),
    .MemWrite(MemWrite), .ALUSrc(ex_mem_1_alusrc_2), .RegWrote(EX_MEM_RegWrite), .Jr(ex_mem_1_jr_2),
    .Jal(ex_mem_1_jal_2), .pc(Data), .ALU(ALUR), .ALU_2(ex_mem_2_alu_2), .RegWrote_2(RegWrite),
    .MemtoReg_2(MemToReg), .pc_2(ex_mem_2_pc_2), .dest(EX_MEM_RD), .dest_2(WrADDr), .clock(clock));  // open: RD2, Zero, RD2_2, Zero_2, ALU2_2, ALU0_2, Jump_2, MemRead_2, MemWrite_2, ALU1_2, RegDest_2, Bracnh_2, ALUSrc_2, Jr_2, Jal_2
  Multiplexer #(.width(32)) multiplexer_12 (
    .in0(ex_mem_2_alu_2), .in1(ex_mem_2_pc_2), .out(WrData), .sel(MemToReg));  // open: en
  // Probe on PC
  // Probe on Branch
  // Probe on Jump
  // Probe on jal
  // Probe on Jr
  // Probe on RegWrite
  // Probe on WrADDr
  // Probe on WrData
  // Probe on MemWrite
  // Probe on Mem_Data

  // Other names for the same wires on the sheet: Bit0_15[5:0] = Bit0_5; Bit0_25[15:0] = {Bit0_15, Bit0_5};
  //   Decode[31:0] = {Bit26_31, Bit0_25, Bit0_15, Bit0_5}; bit_6_10[4:0] = Bit0_15[10:6];
  //   Bit11_15[4:0] = Bit0_15[15:11]; Bit16_20[4:0] = Bit0_25[20:16]; IF_ID_Rt[4:0] = Bit0_25[20:16];
  //   Bit21_25[4:0] = Bit0_25[25:21]; IF_ID_Rs[4:0] = Bit0_25[25:21]; PC_r[31:0] = Jal_value

  // Notes on the sheet:
  //   NOTE:
  //   Only Instruction 2-8 taken
  //   contents of rom_1 (hex, n*v repeats v):
  //   2009fff3 ac090000 8c080000 2009ffff ac090001 8c080001 ac090011 8c0c0011 ac09fffb 8c08fffb
  //   Stall not Needed in this stage
  //   NOTE: If move the jump instruction to stage 3, will need to change Bit:0_25 from Decode stage instead
endmodule

module _32bit (
  input  Add_Sub_control,
  input  [31:0] in_2,
  input  [31:0] in_3,
  output [31:0] out_4,
  output carry_out
);

  wire adder_1_cout, subtractor_1_bout;
  wire [31:0] adder_1_out, subtractor_1_out;

  Adder #(.width(32)) adder_1 (.a(in_2), .b(in_3), .out(adder_1_out), .cout(adder_1_cout));  // open: cin
  Subtractor #(.width(32)) subtractor_1 (
    .a(in_2), .b(in_3), .out(subtractor_1_out), .bout(subtractor_1_bout));  // open: bin
  Multiplexer #(.width(32), .enable("false")) multiplexer_1 (
    .in0(adder_1_out), .in1(subtractor_1_out), .out(out_4), .sel(Add_Sub_control));
  Multiplexer #(.enable("false")) multiplexer_2 (
    .in0(adder_1_cout), .in1(subtractor_1_bout), .out(carry_out), .sel(Add_Sub_control));
endmodule

module ALU (
  input  [2:0] ALUCtl,
  input  [31:0] A,
  input  [31:0] B,
  input  [4:0] Shamt,
  output [31:0] ALUResult,
  output Zero,
  output Overflow
);

  wire and_2_out, and_3_out, comparator_1_lt, not_1_out, not_2_out, not_3_out, or_2_out;
  wire [31:0] Add, And, LessThan, Nor, Or, ShiftLeft, ShiftRight, Sub;

  Adder #(.width(32)) adder_1 (.a(A), .b(B), .out(Add));  // open: cin, cout
  Subtractor #(.width(32)) subtractor_1 (.a(A), .b(B), .out(Sub));  // open: bin, bout
  assign And = A & B;  // AND_Gate and_1, 32 bits wide
  assign Or = A | B;  // OR_Gate or_1, 32 bits wide
  assign Nor = ~(A | B);  // NOR_Gate nor_1, 32 bits wide
  Comparator #(.width(32)) comparator_1 (.a(A), .b(B), .lt(comparator_1_lt));  // open: gt, eq
  assign LessThan = {{31{1'b0}}, comparator_1_lt};  // Bit_Extender bit_extender_1
  Shifter #(.width(32)) shifter_1 (.in(B), .\dist (Shamt), .out(ShiftLeft));
  Shifter #(.width(32), .shift("lr")) shifter_2 (.in(B), .\dist (Shamt), .out(ShiftRight));
  not not_1 (not_1_out, ALUCtl[2]);
  not not_2 (not_2_out, ALUCtl[0]);
  not not_3 (not_3_out, ALUCtl[1]);
  Multiplexer #(.select(3), .width(32), .enable("false")) multiplexer_1 (
    .in0(LessThan), .in1(Sub), .in2(Nor), .in3(And), .in4(Add), .in5(Or), .in6(ShiftLeft), .in7(ShiftRight),
    .out(ALUResult), .sel(ALUCtl));
  and and_2 (and_2_out, not_2_out, not_3_out, ALUCtl[2]);
  and and_3 (and_3_out, not_2_out, ALUCtl[1], not_1_out);
  Overflow overflow_1 (
    .Add(and_2_out), .Sub(and_3_out), .ASign(A[31]), .BSign(B[31]), .ResultSign(ALUResult[31]),
    .Overflow(Overflow));
  or or_2 (or_2_out, ALUResult[0], ALUResult[1], ALUResult[2], ALUResult[3], ALUResult[4], ALUResult[5], ALUResult[6], ALUResult[7], ALUResult[8], ALUResult[9], ALUResult[10], ALUResult[11], ALUResult[12], ALUResult[13], ALUResult[14], ALUResult[15], ALUResult[16], ALUResult[17], ALUResult[18], ALUResult[19], ALUResult[20], ALUResult[21], ALUResult[22], ALUResult[23], ALUResult[24], ALUResult[25], ALUResult[26], ALUResult[27], ALUResult[28], ALUResult[29], ALUResult[30], ALUResult[31]);
  not not_4 (Zero, or_2_out);

  // Other names for the same wires on the sheet: ASign = A[31]; ResultSign = ALUResult[31]; BSign = B[31]
endmodule

module RegFile (
  input  [4:0] WrAddr,
  input  [31:0] WrData,
  input  WrReg,
  input  [4:0] RdAddr1,
  input  [4:0] RdAddr2,
  input  Clock,
  output [31:0] RdData1,
  output [31:0] RdData2
);

  wire and_1_out, and_2_out, comparator_1_eq, comparator_2_eq, comparator_3_eq, comparator_4_eq, not_1_out,
       not_2_out, WrReg0, WrReg1, WrReg2, WrReg3, WrReg4, WrReg5, WrReg6, WrReg7, WrReg8, WrReg9, WrReg10,
       WrReg11, WrReg12, WrReg13, WrReg14, WrReg15, WrReg16, WrReg17, WrReg18, WrReg19, WrReg20, WrReg21,
       WrReg22, WrReg23, WrReg24, WrReg25, WrReg26, WrReg27, WrReg28, WrReg29, WrReg30, WrReg31;
  wire [31:0] multiplexer_1_out, multiplexer_2_out, RegData1, RegData2, RegData3, RegData4, RegData5,
       RegData6, RegData7, RegData8, RegData9, RegData10, RegData11, RegData12, RegData13, RegData14,
       RegData15, RegData16, RegData17, RegData18, RegData19, RegData20, RegData21, RegData22, RegData23,
       RegData24, RegData25, RegData26, RegData27, RegData28, RegData29, RegData30, RegData31;

  Demultiplexer #(.select(5), .enable("false")) demultiplexer_1 (
    .out0(WrReg0), .out1(WrReg1), .out2(WrReg2), .out3(WrReg3), .out4(WrReg4), .out5(WrReg5), .out6(WrReg6),
    .out7(WrReg7), .out8(WrReg8), .out9(WrReg9), .out10(WrReg10), .out11(WrReg11), .out12(WrReg12),
    .out13(WrReg13), .out14(WrReg14), .out15(WrReg15), .out16(WrReg16), .out17(WrReg17), .out18(WrReg18),
    .out19(WrReg19), .out20(WrReg20), .out21(WrReg21), .out22(WrReg22), .out23(WrReg23), .out24(WrReg24),
    .out25(WrReg25), .out26(WrReg26), .out27(WrReg27), .out28(WrReg28), .out29(WrReg29), .out30(WrReg30),
    .out31(WrReg31), .in(WrReg), .sel(WrAddr));
  Register #(.width(32)) Reg4 (.D(WrData), .en(WrReg4), .Q(RegData4), .clk(Clock));  // open: clr
  Register #(.width(32)) Reg8 (.D(WrData), .en(WrReg8), .Q(RegData8), .clk(Clock));  // open: clr
  Register #(.width(32)) Reg12 (.D(WrData), .en(WrReg12), .Q(RegData12), .clk(Clock));  // open: clr
  Register #(.width(32)) Reg16 (.D(WrData), .en(WrReg16), .Q(RegData16), .clk(Clock));  // open: clr
  Register #(.width(32)) Reg20 (.D(WrData), .en(WrReg20), .Q(RegData20), .clk(Clock));  // open: clr
  Register #(.width(32)) Reg24 (.D(WrData), .en(WrReg24), .Q(RegData24), .clk(Clock));  // open: clr
  Register #(.width(32)) Reg28 (.D(WrData), .en(WrReg28), .Q(RegData28), .clk(Clock));  // open: clr
  Register #(.width(32)) Reg1 (.D(WrData), .en(WrReg1), .Q(RegData1), .clk(Clock));  // open: clr
  Register #(.width(32)) Reg5 (.D(WrData), .en(WrReg5), .Q(RegData5), .clk(Clock));  // open: clr
  Register #(.width(32)) Reg9 (.D(WrData), .en(WrReg9), .Q(RegData9), .clk(Clock));  // open: clr
  Register #(.width(32)) Reg13 (.D(WrData), .en(WrReg13), .Q(RegData13), .clk(Clock));  // open: clr
  Register #(.width(32)) Reg17 (.D(WrData), .en(WrReg17), .Q(RegData17), .clk(Clock));  // open: clr
  Register #(.width(32)) Reg21 (.D(WrData), .en(WrReg21), .Q(RegData21), .clk(Clock));  // open: clr
  Register #(.width(32)) Reg25 (.D(WrData), .en(WrReg25), .Q(RegData25), .clk(Clock));  // open: clr
  Register #(.width(32)) Reg29 (.D(WrData), .en(WrReg29), .Q(RegData29), .clk(Clock));  // open: clr
  Register #(.width(32)) Reg2 (.D(WrData), .en(WrReg2), .Q(RegData2), .clk(Clock));  // open: clr
  Register #(.width(32)) Reg6 (.D(WrData), .en(WrReg6), .Q(RegData6), .clk(Clock));  // open: clr
  Register #(.width(32)) Reg10 (.D(WrData), .en(WrReg10), .Q(RegData10), .clk(Clock));  // open: clr
  Register #(.width(32)) Reg14 (.D(WrData), .en(WrReg14), .Q(RegData14), .clk(Clock));  // open: clr
  Register #(.width(32)) Reg18 (.D(WrData), .en(WrReg18), .Q(RegData18), .clk(Clock));  // open: clr
  Register #(.width(32)) Reg22 (.D(WrData), .en(WrReg22), .Q(RegData22), .clk(Clock));  // open: clr
  Register #(.width(32)) Reg26 (.D(WrData), .en(WrReg26), .Q(RegData26), .clk(Clock));  // open: clr
  Register #(.width(32)) Reg30 (.D(WrData), .en(WrReg30), .Q(RegData30), .clk(Clock));  // open: clr
  Register #(.width(32)) Reg3 (.D(WrData), .en(WrReg3), .Q(RegData3), .clk(Clock));  // open: clr
  Register #(.width(32)) Reg7 (.D(WrData), .en(WrReg7), .Q(RegData7), .clk(Clock));  // open: clr
  Register #(.width(32)) Reg11 (.D(WrData), .en(WrReg11), .Q(RegData11), .clk(Clock));  // open: clr
  Register #(.width(32)) Reg15 (.D(WrData), .en(WrReg15), .Q(RegData15), .clk(Clock));  // open: clr
  Register #(.width(32)) Reg19 (.D(WrData), .en(WrReg19), .Q(RegData19), .clk(Clock));  // open: clr
  Register #(.width(32)) Reg23 (.D(WrData), .en(WrReg23), .Q(RegData23), .clk(Clock));  // open: clr
  Register #(.width(32)) Reg27 (.D(WrData), .en(WrReg27), .Q(RegData27), .clk(Clock));  // open: clr
  Register #(.width(32)) Reg31 (.D(WrData), .en(WrReg31), .Q(RegData31), .clk(Clock));  // open: clr
  Multiplexer #(.select(5), .width(32), .enable("false")) multiplexer_1 (
    .in0({32{1'b0}}), .in1(RegData1), .in2(RegData2), .in3(RegData3), .in4(RegData4), .in5(RegData5),
    .in6(RegData6), .in7(RegData7), .in8(RegData8), .in9(RegData9), .in10(RegData10), .in11(RegData11),
    .in12(RegData12), .in13(RegData13), .in14(RegData14), .in15(RegData15), .in16(RegData16),
    .in17(RegData17), .in18(RegData18), .in19(RegData19), .in20(RegData20), .in21(RegData21),
    .in22(RegData22), .in23(RegData23), .in24(RegData24), .in25(RegData25), .in26(RegData26),
    .in27(RegData27), .in28(RegData28), .in29(RegData29), .in30(RegData30), .in31(RegData31),
    .out(multiplexer_1_out), .sel(RdAddr1));
  Multiplexer #(.select(5), .width(32), .enable("false")) multiplexer_2 (
    .in0({32{1'b0}}), .in1(RegData1), .in2(RegData2), .in3(RegData3), .in4(RegData4), .in5(RegData5),
    .in6(RegData6), .in7(RegData7), .in8(RegData8), .in9(RegData9), .in10(RegData10), .in11(RegData11),
    .in12(RegData12), .in13(RegData13), .in14(RegData14), .in15(RegData15), .in16(RegData16),
    .in17(RegData17), .in18(RegData18), .in19(RegData19), .in20(RegData20), .in21(RegData21),
    .in22(RegData22), .in23(RegData23), .in24(RegData24), .in25(RegData25), .in26(RegData26),
    .in27(RegData27), .in28(RegData28), .in29(RegData29), .in30(RegData30), .in31(RegData31),
    .out(multiplexer_2_out), .sel(RdAddr2));
  Multiplexer #(.width(32), .enable("false")) multiplexer_3 (
    .in0(multiplexer_1_out), .in1(WrData), .out(RdData1), .sel(and_1_out));
  Multiplexer #(.width(32), .enable("false")) multiplexer_4 (
    .in0(multiplexer_2_out), .in1(WrData), .out(RdData2), .sel(and_2_out));
  Comparator #(.width(5), .mode("unsigned")) comparator_1 (
    .a(WrAddr), .b(RdAddr1), .eq(comparator_1_eq));  // open: gt, lt
  and and_1 (and_1_out, comparator_1_eq, WrReg, not_1_out);
  Comparator #(.width(5), .mode("unsigned")) comparator_2 (
    .a(WrAddr), .b(RdAddr2), .eq(comparator_2_eq));  // open: gt, lt
  and and_2 (and_2_out, comparator_2_eq, WrReg, not_2_out);
  Comparator #(.width(5), .mode("unsigned")) comparator_3 (
    .a(WrAddr), .b({5{1'b0}}), .eq(comparator_3_eq));  // open: gt, lt
  not not_1 (not_1_out, comparator_3_eq);
  Comparator #(.width(5), .mode("unsigned")) comparator_4 (
    .a(WrAddr), .b({5{1'b0}}), .eq(comparator_4_eq));  // open: gt, lt
  not not_2 (not_2_out, comparator_4_eq);
endmodule

module Overflow (
  input  Add,
  input  Sub,
  input  ASign,
  input  BSign,
  input  ResultSign,
  output Overflow
);

  wire and_1_out, and_2_out, or_1_out, xnor_1_out, xor_1_out, xor_2_out;

  xnor xnor_1 (xnor_1_out, ASign, BSign);
  xor xor_1 (xor_1_out, ASign, BSign);
  and and_1 (and_1_out, xnor_1_out, Add);
  and and_2 (and_2_out, xor_1_out, Sub);
  or or_1 (or_1_out, and_1_out, and_2_out);
  xor xor_2 (xor_2_out, ResultSign, ASign);
  and and_3 (Overflow, or_1_out, xor_2_out);

  // Notes on the sheet:
  //   Overflow occurs when doing addition and sign(A) == sign(B) && sign(result) != sign(A)
  //   Or
  //   Overflow occurs when doing subtraction and sign(A) != sign(B) && sign(result) != sign(A)
endmodule

module RG_EX (
  input  Stall,
  input  ALU2,
  input  ALU1,
  input  Clock,
  input  ALU0,
  input  RegDest,
  input  Jump,
  input  Bracnh,
  input  MemRead,
  input  MemtoReg,
  input  MemWrite,
  input  ALUSrc,
  input  RegWrote,
  input  Jr,
  input  Jal,
  input  [31:0] pc,
  input  [31:0] RD1,
  input  [31:0] RD2,
  input  [31:0] Exted,
  input  [4:0] _11_15,
  input  [4:0] _16_20,
  input  [4:0] SHIFT,
  input  [4:0] _21_25,
  input  [25:0] Bit_0_25,
  output ALU2_2,
  output ALU1_2,
  output ALU0_2,
  output RegDest_2,
  output Jump_2,
  output Bracnh_2,
  output MemRead_2,
  output MemtoReg_2,
  output MemWrite_2,
  output ALUSrc_2,
  output RegWrote_2,
  output Jr_2,
  output Jal_2,
  output [31:0] pc_2,
  output [31:0] RD1_2,
  output [31:0] RD2_2,
  output [31:0] Exted_2,
  output [4:0] _16_20_2,
  output [4:0] _11_15_2,
  output [4:0] SHIFT_2,
  output [4:0] _21_25_2,
  output [25:0] Bit_0_25_2
);

  Register #(.width(1)) register_1 (.D(ALU2), .en(Stall), .Q(ALU2_2), .clk(Clock));  // open: clr
  Register #(.width(1)) register_2 (.D(ALU0), .en(Stall), .Q(ALU0_2), .clk(Clock));  // open: clr
  Register #(.width(1)) register_3 (.D(Jump), .en(Stall), .Q(Jump_2), .clk(Clock));  // open: clr
  Register #(.width(1)) register_4 (.D(MemRead), .en(Stall), .Q(MemRead_2), .clk(Clock));  // open: clr
  Register #(.width(1)) register_5 (.D(MemWrite), .en(Stall), .Q(MemWrite_2), .clk(Clock));  // open: clr
  Register #(.width(1)) register_6 (.D(RegWrote), .en(Stall), .Q(RegWrote_2), .clk(Clock));  // open: clr
  Register #(.width(32)) u_PC (.D(pc), .en(Stall), .Q(pc_2), .clk(Clock));  // open: clr
  Register #(.width(32)) u_RD1 (.D(RD1), .en(Stall), .Q(RD1_2), .clk(Clock));  // open: clr
  Register #(.width(32)) Extend (.D(Exted), .en(Stall), .Q(Exted_2), .clk(Clock));  // open: clr
  Register #(.width(5)) u__16_20 (.D(_16_20), .en(Stall), .Q(_16_20_2), .clk(Clock));  // open: clr
  Register #(.width(5)) u_SHIFT (.D(SHIFT), .en(Stall), .Q(SHIFT_2), .clk(Clock));  // open: clr
  Register #(.width(5)) u__21_25 (.D(_21_25), .en(Stall), .Q(_21_25_2), .clk(Clock));  // open: clr
  Register #(.width(26)) u__21_25_2 (.D(Bit_0_25), .en(Stall), .Q(Bit_0_25_2), .clk(Clock));  // open: clr
  Register #(.width(1)) register_7 (.D(ALU1), .en(Stall), .Q(ALU1_2), .clk(Clock));  // open: clr
  Register #(.width(1)) register_8 (.D(RegDest), .en(Stall), .Q(RegDest_2), .clk(Clock));  // open: clr
  Register #(.width(1)) register_9 (.D(Bracnh), .en(Stall), .Q(Bracnh_2), .clk(Clock));  // open: clr
  Register #(.width(1)) register_10 (.D(MemtoReg), .en(Stall), .Q(MemtoReg_2), .clk(Clock));  // open: clr
  Register #(.width(1)) register_11 (.D(ALUSrc), .en(Stall), .Q(ALUSrc_2), .clk(Clock));  // open: clr
  Register #(.width(1)) register_12 (.D(Jr), .en(Stall), .Q(Jr_2), .clk(Clock));  // open: clr
  Register #(.width(1)) register_13 (.D(Jal), .en(Stall), .Q(Jal_2), .clk(Clock));  // open: clr
  Register #(.width(32)) u_RD2 (.D(RD2), .en(Stall), .Q(RD2_2), .clk(Clock));  // open: clr
  Register #(.width(5)) u__11_15 (.D(_11_15), .en(Stall), .Q(_11_15_2), .clk(Clock));  // open: clr
endmodule

module IF_D (
  input  NotStall,
  input  [31:0] PC,
  input  Clock,
  input  [31:0] PC_plus,
  input  Squish,
  output [31:0] IR,
  output [31:0] PC_plus_2,
  output Squish_2
);

  // Probe on PC
  // Probe on IR
  Register #(.width(32)) u_IR (.D(PC), .en(NotStall), .Q(IR), .clk(Clock));  // open: clr
  Register #(.width(32)) PC_4 (.D(PC_plus), .en(NotStall), .Q(PC_plus_2), .clk(Clock));  // open: clr
  Register #(.width(1)) u_Squish (.D(Squish), .Q(Squish_2), .clk(Clock));  // open: en, clr
endmodule

module EX_MEM (
  input  ALU2,
  input  ALU1,
  input  clock,
  input  ALU0,
  input  RegDest,
  input  Jump,
  input  Bracnh,
  input  MemRead,
  input  MemtoReg,
  input  MemWrite,
  input  ALUSrc,
  input  RegWrote,
  input  Jr,
  input  Jal,
  input  [31:0] pc,
  input  [31:0] ALU,
  input  [31:0] RD2,
  input  Zero,
  input  [4:0] dest,
  output ALU2_2,
  output ALU1_2,
  output ALU0_2,
  output RegDest_2,
  output Jump_2,
  output Bracnh_2,
  output MemRead_2,
  output MemtoReg_2,
  output MemWrite_2,
  output ALUSrc_2,
  output RegWrote_2,
  output Jr_2,
  output Jal_2,
  output [31:0] pc_2,
  output [31:0] ALU_2,
  output [31:0] RD2_2,
  output Zero_2,
  output [4:0] dest_2
);

  Register #(.width(1)) register_1 (.D(ALU2), .Q(ALU2_2), .clk(clock));  // open: en, clr
  Register #(.width(1)) register_2 (.D(ALU0), .Q(ALU0_2), .clk(clock));  // open: en, clr
  Register #(.width(1)) register_3 (.D(Jump), .Q(Jump_2), .clk(clock));  // open: en, clr
  Register #(.width(1)) register_4 (.D(MemRead), .Q(MemRead_2), .clk(clock));  // open: en, clr
  Register #(.width(1)) register_5 (.D(MemWrite), .Q(MemWrite_2), .clk(clock));  // open: en, clr
  Register #(.width(1)) register_6 (.D(RegWrote), .Q(RegWrote_2), .clk(clock));  // open: en, clr
  Register #(.width(32)) u_PC (.D(pc), .Q(pc_2), .clk(clock));  // open: en, clr
  Register #(.width(32)) u_ALU (.D(ALU), .Q(ALU_2), .clk(clock));  // open: en, clr
  Register #(.width(1)) Extend (.D(Zero), .Q(Zero_2), .clk(clock));  // open: en, clr
  Register #(.width(5)) u_dest (.D(dest), .Q(dest_2), .clk(clock));  // open: en, clr
  Register #(.width(1)) register_7 (.D(ALU1), .Q(ALU1_2), .clk(clock));  // open: en, clr
  Register #(.width(1)) register_8 (.D(RegDest), .Q(RegDest_2), .clk(clock));  // open: en, clr
  Register #(.width(1)) register_9 (.D(Bracnh), .Q(Bracnh_2), .clk(clock));  // open: en, clr
  Register #(.width(1)) register_10 (.D(MemtoReg), .Q(MemtoReg_2), .clk(clock));  // open: en, clr
  Register #(.width(1)) register_11 (.D(ALUSrc), .Q(ALUSrc_2), .clk(clock));  // open: en, clr
  Register #(.width(1)) register_12 (.D(Jr), .Q(Jr_2), .clk(clock));  // open: en, clr
  Register #(.width(1)) register_13 (.D(Jal), .Q(Jal_2), .clk(clock));  // open: en, clr
  Register #(.width(32)) u_RD2 (.D(RD2), .Q(RD2_2), .clk(clock));  // open: en, clr
endmodule

// ForwardA
module ForwardingUnit (
  input  [4:0] ID_EX_RS,
  input  [4:0] ID_EX_RT,
  input  EX_MEM_RegWrite,
  input  [4:0] EX_MEM_RegRd,
  input  MEM_WB_RegWrite,
  input  [4:0] MEM_WB_RegRd,
  input  EX_MEM_MemWr,
  output [1:0] ForwardA,
  output [1:0] ForwardB,
  output MemForward
);

  wire comparator_1_eq, comparator_2_eq, comparator_3_eq, comparator_4_eq, comparator_5_eq, comparator_6_eq,
       comparator_7_eq, comparator_8_eq, comparator_9_eq, not_1_out, not_2_out, not_3_out, not_4_out,
       not_5_out, not_6_out;

  Comparator #(.width(5)) comparator_1 (.a(MEM_WB_RegRd), .b(EX_MEM_RegRd), .eq(comparator_1_eq));  // open: gt, lt
  Comparator #(.width(5)) comparator_2 (.a(EX_MEM_RegRd), .b({5{1'b0}}), .eq(comparator_2_eq));  // open: gt, lt
  Comparator #(.width(5)) comparator_3 (.a(EX_MEM_RegRd), .b(ID_EX_RS), .eq(comparator_3_eq));  // open: gt, lt
  Comparator #(.width(5)) comparator_4 (.a(ID_EX_RS), .b(MEM_WB_RegRd), .eq(comparator_4_eq));  // open: gt, lt
  Comparator #(.width(5)) comparator_5 (.a(MEM_WB_RegRd), .b({5{1'b0}}), .eq(comparator_5_eq));  // open: gt, lt
  Comparator #(.width(5)) comparator_6 (.a(EX_MEM_RegRd), .b(ID_EX_RT), .eq(comparator_6_eq));  // open: gt, lt
  Comparator #(.width(5)) comparator_7 (.a(EX_MEM_RegRd), .b({5{1'b0}}), .eq(comparator_7_eq));  // open: gt, lt
  Comparator #(.width(5)) comparator_8 (.a(MEM_WB_RegRd), .b(ID_EX_RT), .eq(comparator_8_eq));  // open: gt, lt
  Comparator #(.width(5)) comparator_9 (.a(MEM_WB_RegRd), .b({5{1'b0}}), .eq(comparator_9_eq));  // open: gt, lt
  not not_1 (not_1_out, comparator_2_eq);
  not not_2 (not_2_out, comparator_5_eq);
  not not_3 (not_3_out, comparator_7_eq);
  not not_4 (not_4_out, ForwardB[1]);
  not not_5 (not_5_out, comparator_9_eq);
  and and_1 (ForwardA[1], EX_MEM_RegWrite, not_1_out, comparator_3_eq);
  not not_6 (not_6_out, ForwardA[1]);
  and and_2 (ForwardA[0], not_6_out, MEM_WB_RegWrite, comparator_4_eq, not_2_out);
  and and_3 (ForwardB[1], EX_MEM_RegWrite, comparator_6_eq, not_3_out);
  and and_4 (ForwardB[0], not_4_out, comparator_8_eq, not_5_out, MEM_WB_RegWrite);
  and and_5 (MemForward, not_5_out, comparator_1_eq, MEM_WB_RegWrite, EX_MEM_MemWr);
endmodule

module test (
  input  [4:0] ID_EX_RS,
  input  [4:0] ID_EX_RT,
  input  EX_MEM_RegWrite,
  input  [4:0] EX_MEM_RegRd,
  input  MEM_WB_RegWrite,
  input  [4:0] MEM_WB_RegRd,
  output [1:0] ForwardA,
  output [1:0] ForwardB
);

  wire comparator_1_eq, comparator_2_eq, comparator_3_eq, comparator_4_eq, comparator_5_eq, comparator_6_eq,
       comparator_7_eq, comparator_8_eq, not_1_out, not_2_out, not_3_out, not_4_out, not_5_out, not_6_out;

  Comparator #(.width(5)) comparator_1 (.a(EX_MEM_RegRd), .b({5{1'b0}}), .eq(comparator_1_eq));  // open: gt, lt
  Comparator #(.width(5)) comparator_2 (.a(EX_MEM_RegRd), .b(ID_EX_RS), .eq(comparator_2_eq));  // open: gt, lt
  Comparator #(.width(5)) comparator_3 (.a(ID_EX_RS), .b(MEM_WB_RegRd), .eq(comparator_3_eq));  // open: gt, lt
  Comparator #(.width(5)) comparator_4 (.a(MEM_WB_RegRd), .b({5{1'b0}}), .eq(comparator_4_eq));  // open: gt, lt
  Comparator #(.width(5)) comparator_5 (.a(EX_MEM_RegRd), .b(ID_EX_RT), .eq(comparator_5_eq));  // open: gt, lt
  Comparator #(.width(5)) comparator_6 (.a(EX_MEM_RegRd), .b({5{1'b0}}), .eq(comparator_6_eq));  // open: gt, lt
  Comparator #(.width(5)) comparator_7 (.a(MEM_WB_RegRd), .b(ID_EX_RT), .eq(comparator_7_eq));  // open: gt, lt
  Comparator #(.width(5)) comparator_8 (.a(MEM_WB_RegRd), .b({5{1'b0}}), .eq(comparator_8_eq));  // open: gt, lt
  not not_1 (not_1_out, comparator_1_eq);
  not not_2 (not_2_out, comparator_4_eq);
  not not_3 (not_3_out, comparator_6_eq);
  not not_4 (not_4_out, comparator_5_eq);
  not not_5 (not_5_out, comparator_8_eq);
  and and_1 (ForwardA[1], EX_MEM_RegWrite, not_1_out, comparator_2_eq);
  not not_6 (not_6_out, comparator_2_eq);
  and and_2 (ForwardA[0], not_6_out, MEM_WB_RegWrite, comparator_3_eq, not_2_out);
  and and_3 (ForwardB[1], EX_MEM_RegWrite, comparator_5_eq, not_3_out);
  and and_4 (ForwardB[0], not_4_out, comparator_7_eq, not_5_out, MEM_WB_RegWrite);
endmodule

module Hazard_Detect (
  input  ID_EX_MemRead,
  input  [4:0] ID_EX_Rt,
  input  [4:0] IF_ID_Rs,
  input  [4:0] IF_ID_Rt,
  input  LW_Instruction,
  output IF_ID_Write,
  output PC_Write,
  output Stall_Control,
  output Stalling_Now
);

  wire and_1_out, comparator_1_eq, comparator_2_eq, not_1_out, or_1_out;

  not not_1 (not_1_out, LW_Instruction);
  Comparator #(.width(5)) comparator_1 (.a(ID_EX_Rt), .b(IF_ID_Rs), .eq(comparator_1_eq));  // open: gt, lt
  Comparator #(.width(5)) comparator_2 (.a(ID_EX_Rt), .b(IF_ID_Rt), .eq(comparator_2_eq));  // open: gt, lt
  or or_1 (or_1_out, comparator_1_eq, and_1_out);
  and and_1 (and_1_out, comparator_2_eq, not_1_out);
  and and_2 (Stall_Control, ID_EX_MemRead, or_1_out);
  not not_2 (IF_ID_Write, Stall_Control);

  assign PC_Write = IF_ID_Write;
  assign Stalling_Now = Stall_Control;

  // Notes on the sheet:
  //   The Not gate is there for the two Write signals because, in all other cases we want the registered to be ENABLED which are driven by these..
endmodule

module Control_Unit (
  input  I31,
  input  I30,
  input  I29,
  input  I28,
  input  I27,
  input  I26,
  input  I5,
  input  I4,
  input  I3,
  input  I2,
  input  I1,
  input  I0,
  output ALU2,
  output ALU1,
  output ALU0,
  output RegDst,
  output Jump,
  output Branch,
  output MemRead,
  output MemToReg,
  output MemWrite,
  output ALUSrc,
  output RegWrite,
  output Jr,
  output Jal
);

  wire and_1_out, and_2_out, and_3_out, and_4_out, and_5_out, and_6_out, and_7_out, and_8_out, and_9_out,
       and_10_out, and_11_out, and_12_out, and_13_out, and_14_out, and_15_out, and_16_out, and_17_out,
       and_23_out, and_24_out, and_25_out, and_26_out, and_27_out, and_28_out, and_29_out, and_30_out,
       and_31_out, and_32_out, and_33_out, and_34_out, and_35_out, and_36_out, not_1_out, not_2_out,
       not_3_out, not_4_out, not_5_out, not_6_out, not_7_out, not_8_out, not_9_out, not_10_out, not_11_out,
       not_12_out, not_13_out, not_14_out, not_15_out, not_16_out, not_17_out, not_18_out, not_19_out,
       not_20_out, not_21_out, not_22_out, not_23_out, not_24_out, not_25_out, not_26_out, not_27_out,
       not_28_out, not_29_out, not_30_out, not_31_out, not_32_out, not_33_out, not_34_out, not_35_out,
       not_36_out, not_37_out, not_38_out, not_39_out, not_40_out, not_41_out, not_42_out, not_43_out,
       not_44_out, not_45_out, not_46_out, not_47_out, not_48_out, not_49_out, not_50_out, not_51_out,
       not_52_out, not_53_out, not_54_out, not_55_out, not_56_out, not_57_out, not_58_out, not_59_out,
       not_60_out, not_61_out, not_62_out, not_63_out, not_64_out, not_65_out, not_66_out, not_67_out,
       not_68_out, not_69_out, not_70_out, not_71_out, not_72_out, not_73_out, not_74_out, not_75_out,
       not_76_out, not_77_out, not_78_out, not_79_out, not_80_out, not_81_out, not_82_out, not_83_out,
       not_84_out, not_85_out, not_86_out, not_87_out, not_88_out, not_89_out, not_90_out, not_91_out,
       not_92_out, not_93_out, not_94_out, not_95_out, not_96_out, not_97_out, not_98_out, not_99_out,
       not_100_out, not_101_out, not_102_out, not_103_out, not_104_out, not_105_out, not_106_out,
       not_107_out, not_108_out, not_109_out, not_110_out, not_111_out, not_112_out, not_113_out,
       not_114_out, not_115_out, not_116_out, not_117_out, not_118_out, not_119_out, not_120_out,
       not_121_out, not_122_out, not_123_out, not_124_out, not_125_out, not_126_out, not_127_out,
       not_128_out, not_129_out, not_130_out, not_131_out, not_132_out, not_133_out, not_134_out,
       not_135_out, not_136_out, not_137_out, not_138_out, not_139_out, not_140_out, not_141_out,
       not_142_out, not_143_out, not_144_out, not_145_out, not_146_out, not_147_out, not_148_out,
       not_149_out, not_150_out, not_151_out, not_152_out, not_153_out, not_154_out, not_155_out,
       not_156_out, not_157_out, not_158_out, not_159_out, not_160_out, not_161_out, not_162_out,
       not_163_out, not_164_out, not_165_out, not_166_out, not_167_out, not_168_out, not_169_out,
       not_170_out, not_171_out, not_172_out, not_173_out, not_174_out, not_175_out, not_176_out,
       not_177_out, not_178_out, not_179_out, not_180_out, not_181_out, not_182_out, not_183_out,
       not_184_out, not_185_out, not_186_out, not_187_out, not_188_out, not_189_out, not_190_out,
       not_191_out, not_192_out, not_193_out, not_194_out, not_195_out, not_196_out, not_197_out,
       not_198_out, not_199_out, not_200_out, not_201_out, not_202_out, not_203_out, not_204_out,
       not_205_out, not_206_out, not_207_out, not_208_out, not_209_out, not_210_out, not_211_out,
       not_212_out, not_213_out, not_214_out, not_215_out, not_216_out, not_217_out, not_218_out,
       not_219_out, not_220_out, not_221_out, not_222_out, not_223_out, not_224_out, not_225_out,
       not_226_out, not_227_out, not_228_out, not_229_out, not_230_out, not_231_out, not_232_out,
       not_233_out, not_234_out, not_235_out, not_236_out, not_237_out, not_238_out, not_239_out;

  not not_1 (not_1_out, I31);
  not not_2 (not_2_out, I30);
  not not_3 (not_3_out, I28);
  not not_4 (not_4_out, I27);
  not not_5 (not_5_out, I26);
  not not_6 (not_6_out, I4);
  not not_7 (not_7_out, I3);
  not not_8 (not_8_out, I2);
  not not_9 (not_9_out, I1);
  not not_10 (not_10_out, I0);
  not not_11 (not_11_out, I31);
  not not_12 (not_12_out, I30);
  not not_13 (not_13_out, I28);
  not not_14 (not_14_out, I27);
  not not_15 (not_15_out, I26);
  not not_16 (not_16_out, I4);
  not not_17 (not_17_out, I3);
  not not_18 (not_18_out, I1);
  not not_19 (not_19_out, I31);
  not not_20 (not_20_out, I30);
  not not_21 (not_21_out, I29);
  not not_22 (not_22_out, I28);
  not not_23 (not_23_out, I27);
  not not_24 (not_24_out, I26);
  not not_25 (not_25_out, I5);
  not not_26 (not_26_out, I4);
  not not_27 (not_27_out, I3);
  not not_28 (not_28_out, I2);
  not not_29 (not_29_out, I1);
  not not_30 (not_30_out, I0);
  not not_31 (not_31_out, I31);
  not not_32 (not_32_out, I30);
  not not_33 (not_33_out, I29);
  not not_34 (not_34_out, I28);
  not not_35 (not_35_out, I27);
  not not_36 (not_36_out, I26);
  not not_37 (not_37_out, I5);
  not not_38 (not_38_out, I4);
  not not_39 (not_39_out, I3);
  not not_40 (not_40_out, I2);
  not not_41 (not_41_out, I0);
  not not_42 (not_42_out, I31);
  not not_43 (not_43_out, I30);
  not not_44 (not_44_out, I28);
  not not_45 (not_45_out, I27);
  not not_46 (not_46_out, I26);
  not not_47 (not_47_out, I31);
  not not_48 (not_48_out, I30);
  not not_49 (not_49_out, I27);
  not not_50 (not_50_out, I30);
  not not_51 (not_51_out, I28);
  not not_52 (not_52_out, I31);
  not not_53 (not_53_out, I30);
  not not_54 (not_54_out, I29);
  not not_55 (not_55_out, I28);
  not not_56 (not_56_out, I27);
  not not_57 (not_57_out, I26);
  not not_58 (not_58_out, I4);
  not not_59 (not_59_out, I3);
  not not_60 (not_60_out, I1);
  not not_61 (not_61_out, I0);
  not not_62 (not_62_out, I31);
  not not_63 (not_63_out, I30);
  not not_64 (not_64_out, I29);
  not not_65 (not_65_out, I28);
  not not_66 (not_66_out, I27);
  not not_67 (not_67_out, I26);
  not not_68 (not_68_out, I4);
  not not_69 (not_69_out, I3);
  not not_70 (not_70_out, I31);
  not not_71 (not_71_out, I30);
  not not_72 (not_72_out, I29);
  not not_73 (not_73_out, I28);
  not not_74 (not_74_out, I27);
  not not_75 (not_75_out, I26);
  not not_76 (not_76_out, I5);
  not not_77 (not_77_out, I4);
  not not_78 (not_78_out, I3);
  not not_79 (not_79_out, I2);
  not not_80 (not_80_out, I1);
  not not_81 (not_81_out, I0);
  not not_82 (not_82_out, I31);
  not not_83 (not_83_out, I30);
  not not_84 (not_84_out, I29);
  not not_85 (not_85_out, I28);
  not not_86 (not_86_out, I27);
  not not_87 (not_87_out, I26);
  not not_88 (not_88_out, I5);
  not not_89 (not_89_out, I4);
  not not_90 (not_90_out, I3);
  not not_91 (not_91_out, I2);
  not not_92 (not_92_out, I0);
  not not_93 (not_93_out, I31);
  not not_94 (not_94_out, I30);
  not not_95 (not_95_out, I27);
  not not_96 (not_96_out, I26);
  not not_97 (not_97_out, I31);
  not not_98 (not_98_out, I30);
  not not_99 (not_99_out, I29);
  not not_100 (not_100_out, I27);
  not not_101 (not_101_out, I26);
  not not_102 (not_102_out, I4);
  not not_103 (not_103_out, I3);
  not not_104 (not_104_out, I2);
  not not_105 (not_105_out, I0);
  not not_106 (not_106_out, I31);
  not not_107 (not_107_out, I30);
  not not_108 (not_108_out, I29);
  not not_109 (not_109_out, I27);
  not not_110 (not_110_out, I26);
  not not_111 (not_111_out, I4);
  not not_112 (not_112_out, I3);
  not not_113 (not_113_out, I1);
  not not_114 (not_114_out, I31);
  not not_115 (not_115_out, I30);
  not not_116 (not_116_out, I29);
  not not_117 (not_117_out, I28);
  not not_118 (not_118_out, I27);
  not not_119 (not_119_out, I26);
  not not_120 (not_120_out, I5);
  not not_121 (not_121_out, I4);
  not not_122 (not_122_out, I3);
  not not_123 (not_123_out, I2);
  not not_124 (not_124_out, I0);
  not not_125 (not_125_out, I31);
  not not_126 (not_126_out, I30);
  not not_127 (not_127_out, I27);
  not not_128 (not_128_out, I26);
  not not_129 (not_129_out, I31);
  not not_130 (not_130_out, I30);
  not not_131 (not_131_out, I27);
  not not_132 (not_132_out, I31);
  not not_133 (not_133_out, I30);
  not not_134 (not_134_out, I29);
  not not_135 (not_135_out, I28);
  not not_136 (not_136_out, I27);
  not not_137 (not_137_out, I26);
  not not_138 (not_138_out, I31);
  not not_139 (not_139_out, I30);
  not not_140 (not_140_out, I29);
  not not_141 (not_141_out, I28);
  not not_142 (not_142_out, I31);
  not not_143 (not_143_out, I30);
  not not_144 (not_144_out, I29);
  not not_145 (not_145_out, I27);
  not not_146 (not_146_out, I26);
  not not_147 (not_147_out, I30);
  not not_148 (not_148_out, I29);
  not not_149 (not_149_out, I28);
  not not_150 (not_150_out, I30);
  not not_151 (not_151_out, I28);
  not not_152 (not_152_out, I31);
  not not_153 (not_153_out, I30);
  not not_154 (not_154_out, I27);
  not not_155 (not_155_out, I26);
  not not_156 (not_156_out, I31);
  not not_157 (not_157_out, I30);
  not not_158 (not_158_out, I27);
  not not_159 (not_159_out, I30);
  not not_160 (not_160_out, I28);
  not not_161 (not_161_out, I31);
  not not_162 (not_162_out, I30);
  not not_163 (not_163_out, I28);
  not not_164 (not_164_out, I27);
  not not_165 (not_165_out, I26);
  not not_166 (not_166_out, I3);
  not not_167 (not_167_out, I31);
  not not_168 (not_168_out, I30);
  not not_169 (not_169_out, I28);
  not not_170 (not_170_out, I27);
  not not_171 (not_171_out, I26);
  not not_172 (not_172_out, I31);
  not not_173 (not_173_out, I30);
  not not_174 (not_174_out, I28);
  not not_175 (not_175_out, I27);
  not not_176 (not_176_out, I26);
  not not_177 (not_177_out, I31);
  not not_178 (not_178_out, I30);
  not not_179 (not_179_out, I28);
  not not_180 (not_180_out, I27);
  not not_181 (not_181_out, I26);
  not not_182 (not_182_out, I31);
  not not_183 (not_183_out, I30);
  not not_184 (not_184_out, I28);
  not not_185 (not_185_out, I27);
  not not_186 (not_186_out, I26);
  not not_187 (not_187_out, I31);
  not not_188 (not_188_out, I30);
  not not_189 (not_189_out, I28);
  not not_190 (not_190_out, I27);
  not not_191 (not_191_out, I26);
  not not_192 (not_192_out, I30);
  not not_193 (not_193_out, I29);
  not not_194 (not_194_out, I28);
  not not_195 (not_195_out, I31);
  not not_196 (not_196_out, I30);
  not not_197 (not_197_out, I27);
  not not_198 (not_198_out, I26);
  not not_199 (not_199_out, I31);
  not not_200 (not_200_out, I30);
  not not_201 (not_201_out, I27);
  not not_202 (not_202_out, I31);
  not not_203 (not_203_out, I30);
  not not_204 (not_204_out, I29);
  not not_205 (not_205_out, I28);
  not not_206 (not_206_out, I27);
  not not_207 (not_207_out, I26);
  not not_208 (not_208_out, I5);
  not not_209 (not_209_out, I4);
  not not_210 (not_210_out, I3);
  not not_211 (not_211_out, I2);
  not not_212 (not_212_out, I1);
  not not_213 (not_213_out, I0);
  not not_214 (not_214_out, I31);
  not not_215 (not_215_out, I30);
  not not_216 (not_216_out, I29);
  not not_217 (not_217_out, I28);
  not not_218 (not_218_out, I27);
  not not_219 (not_219_out, I26);
  not not_220 (not_220_out, I5);
  not not_221 (not_221_out, I4);
  not not_222 (not_222_out, I3);
  not not_223 (not_223_out, I2);
  not not_224 (not_224_out, I0);
  not not_225 (not_225_out, I31);
  not not_226 (not_226_out, I30);
  not not_227 (not_227_out, I29);
  not not_228 (not_228_out, I28);
  not not_229 (not_229_out, I27);
  not not_230 (not_230_out, I26);
  not not_231 (not_231_out, I5);
  not not_232 (not_232_out, I4);
  not not_233 (not_233_out, I2);
  not not_234 (not_234_out, I1);
  not not_235 (not_235_out, I0);
  not not_236 (not_236_out, I31);
  not not_237 (not_237_out, I30);
  not not_238 (not_238_out, I29);
  not not_239 (not_239_out, I28);
  and and_1 (and_1_out, not_1_out, not_2_out, not_3_out, not_4_out, not_5_out, I5, not_6_out, not_7_out, not_8_out, not_9_out, not_10_out);
  and and_2 (and_2_out, not_11_out, not_12_out, not_13_out, not_14_out, not_15_out, I5, not_16_out, not_17_out, I2, not_18_out, I0);
  and and_3 (and_3_out, not_19_out, not_20_out, not_21_out, not_22_out, not_23_out, not_24_out, not_25_out, not_26_out, not_27_out, not_28_out, not_29_out, not_30_out);
  and and_4 (and_4_out, not_31_out, not_32_out, not_33_out, not_34_out, not_35_out, not_36_out, not_37_out, not_38_out, not_39_out, not_40_out, I1, not_41_out);
  and and_5 (and_5_out, not_42_out, not_43_out, I29, not_44_out, not_45_out, not_46_out);
  and and_6 (and_6_out, not_47_out, not_48_out, I29, I28, not_49_out, I26);
  and and_7 (and_7_out, I31, not_50_out, not_51_out, I27, I26);
  and and_8 (and_8_out, not_52_out, not_53_out, not_54_out, not_55_out, not_56_out, not_57_out, I5, not_58_out, not_59_out, I2, not_60_out, not_61_out);
  and and_9 (and_9_out, not_62_out, not_63_out, not_64_out, not_65_out, not_66_out, not_67_out, I5, not_68_out, not_69_out, I2, I1, I0);
  and and_10 (and_10_out, not_70_out, not_71_out, not_72_out, not_73_out, not_74_out, not_75_out, not_76_out, not_77_out, not_78_out, not_79_out, not_80_out, not_81_out);
  and and_11 (and_11_out, not_82_out, not_83_out, not_84_out, not_85_out, not_86_out, not_87_out, not_88_out, not_89_out, not_90_out, not_91_out, I1, not_92_out);
  and and_12 (and_12_out, not_93_out, not_94_out, I29, I28, not_95_out, not_96_out);
  and and_13 (and_13_out, not_97_out, not_98_out, not_99_out, not_100_out, not_101_out, I5, not_102_out, not_103_out, not_104_out, I1, not_105_out);
  and and_14 (and_14_out, not_106_out, not_107_out, not_108_out, not_109_out, not_110_out, I5, not_111_out, not_112_out, I2, not_113_out);
  and and_15 (and_15_out, not_114_out, not_115_out, not_116_out, not_117_out, not_118_out, not_119_out, not_120_out, not_121_out, not_122_out, not_123_out, I1, not_124_out);
  and and_16 (and_16_out, not_125_out, not_126_out, I28, not_127_out, not_128_out);
  and and_17 (and_17_out, not_129_out, not_130_out, I29, I28, not_131_out);
  and and_18 (RegDst, not_132_out, not_133_out, not_134_out, not_135_out, not_136_out, not_137_out);
  and and_19 (Jump, not_138_out, not_139_out, not_140_out, not_141_out, I27);
  and and_20 (Branch, not_142_out, not_143_out, not_144_out, I28, not_145_out, not_146_out);
  and and_21 (MemRead, I31, not_147_out, not_148_out, not_149_out, I27, I26);
  and and_22 (MemWrite, I31, not_150_out, I29, not_151_out, I27, I26);
  and and_23 (and_23_out, not_152_out, not_153_out, I29, not_154_out, not_155_out);
  or or_1 (ALUSrc, and_23_out, and_24_out, and_25_out);
  and and_24 (and_24_out, not_156_out, not_157_out, I29, I28, not_158_out);
  and and_25 (and_25_out, I31, not_159_out, not_160_out, I27, I26);
  and and_26 (and_26_out, not_161_out, not_162_out, not_163_out, not_164_out, not_165_out, not_166_out);
  and and_27 (and_27_out, not_167_out, not_168_out, not_169_out, not_170_out, not_171_out, I0);
  and and_28 (and_28_out, not_172_out, not_173_out, not_174_out, not_175_out, not_176_out, I1);
  and and_29 (and_29_out, not_177_out, not_178_out, not_179_out, not_180_out, not_181_out, I2);
  and and_30 (and_30_out, not_182_out, not_183_out, not_184_out, not_185_out, not_186_out, I4);
  and and_31 (and_31_out, not_187_out, not_188_out, not_189_out, not_190_out, not_191_out, I5);
  and and_32 (and_32_out, not_192_out, not_193_out, not_194_out, I27, I26);
  and and_33 (and_33_out, not_195_out, not_196_out, I29, not_197_out, not_198_out);
  and and_34 (and_34_out, not_199_out, not_200_out, I29, I28, not_201_out);
  and and_35 (and_35_out, not_202_out, not_203_out, not_204_out, not_205_out, not_206_out, not_207_out, not_208_out, not_209_out, not_210_out, not_211_out, not_212_out, not_213_out);
  and and_36 (and_36_out, not_214_out, not_215_out, not_216_out, not_217_out, not_218_out, not_219_out, not_220_out, not_221_out, not_222_out, not_223_out, I1, not_224_out);
  and and_37 (Jr, not_225_out, not_226_out, not_227_out, not_228_out, not_229_out, not_230_out, not_231_out, not_232_out, I3, not_233_out, not_234_out, not_235_out);
  and and_38 (Jal, not_236_out, not_237_out, not_238_out, not_239_out, I27, I26);
  or or_2 (ALU2, and_1_out, and_2_out, and_3_out, and_4_out, and_5_out, and_6_out, and_7_out);
  or or_3 (ALU1, and_8_out, and_9_out, and_10_out, and_11_out, and_12_out);
  or or_4 (ALU0, and_13_out, and_14_out, and_15_out, and_16_out, and_17_out);
  or or_5 (RegWrite, and_26_out, and_27_out, and_28_out, and_29_out, and_30_out, and_31_out, and_32_out, and_33_out, and_34_out, and_35_out, and_36_out);

  assign MemToReg = MemRead;
endmodule

module SignExtend (
  input  [15:0] Input,
  output [31:0] Output
);


  assign Output = {{17{Input[15]}}, Input[14:0]};
endmodule

module Shift_Left2 (
  input  [31:0] Input,
  output [31:0] Output
);

  Shifter #(.width(32)) shifter_1 (.in(Input), .\dist (5'b00010), .out(Output));

  // Notes on the sheet:
  //   Shift by 2 Bits only
endmodule

module Add (
  input  [31:0] A,
  input  [31:0] B,
  output [31:0] Output,
  output Overflow
);

  // SingleCycle_ALU alu_1: pin names not known; wires that end beside it: A, B, {5{1'b0}}, 3'b100, Output, Overflow

  // Notes on the sheet:
  //   ADD function: 101
endmodule

module memory (
  input  [7:0] addr,
  input  clock,
  input  reset,
  input  memWrite,
  input  memRead,
  input  [31:0] data_in,
  output [31:0] data,
  output miss,
  output [9:0] misses,
  output [9:0] Cache_accesses,
  output [9:0] RAM_accesses
);

  wire and_1_out, and_2_out, and_3_out, multiplexer_1_out, not_1_out, or_1_out, or_2_out, or_3_out;
  wire [31:0] cacheDataT, multiplexer_2_out, ramDataT;

  not not_1 (not_1_out, miss);
  Multiplexer multiplexer_1 (.in0(miss), .in1(1'b0), .out(multiplexer_1_out), .sel(memWrite));  // open: en
  Multiplexer #(.width(32)) multiplexer_2 (
    .in0(data_in), .in1(ramDataT), .out(multiplexer_2_out), .sel(multiplexer_1_out));  // open: en
  or or_1 (or_1_out, memWrite, memRead);
  or or_2 (or_2_out, not_1_out, memWrite);
  or or_3 (or_3_out, miss, memWrite);
  Counter #(.width(10), .max('h3ff)) counter_1 (
    .count(and_1_out), .Q(Cache_accesses), .clk(clock), .clr(reset));  // open: load, D, carry
  and and_1 (and_1_out, or_1_out, or_2_out);
  Counter #(.width(10), .max('h3ff)) counter_2 (
    .count(and_2_out), .Q(RAM_accesses), .clk(clock), .clr(reset));  // open: load, D, carry
  and and_2 (and_2_out, or_1_out, or_3_out);
  cache cache_1 (
    .addr(addr), .data_in(multiplexer_2_out), .memRead(memRead), .clock(clock), .reset(reset),
    .memWrite(memWrite), .miss(miss), .data_out(cacheDataT));
  Multiplexer #(.width(32)) multiplexer_3 (.in0(cacheDataT), .in1(ramDataT), .out(data), .sel(miss));  // open: en
  Counter #(.width(10), .max('h3ff)) counter_3 (
    .count(miss), .Q(misses), .clk(clock), .clr(reset));  // open: load, D, carry
  RAM #(.dataWidth(32), .bus("separate")) ram_1 (
    .addr(addr), .din(data_in), .data(ramDataT), .str(memWrite), .clk(clock), .ld(memRead), .clr(and_3_out));  // open: sel
  and and_3 (and_3_out, clock, reset);

  // Other names for the same wires on the sheet: addrT[7:0] = addr; clockT = clock; data_inT[31:0] = data_in;
  //   memReadT = memRead; memWriteT = memWrite; missT = miss; resetT = reset

  // Notes on the sheet:
  //   Entradas e saída
  //   Cache
  //   Contadores
  //   Sinais de controle
  //   Memória Principal
endmodule

module cache (
  input  [7:0] addr,
  input  memWrite,
  input  memRead,
  input  [31:0] data_in,
  input  clock,
  input  reset,
  output miss,
  output [31:0] data_out
);

  wire _0_miss, _1_miss, _2_miss, _3_miss, demultiplexer_1_out0, demultiplexer_1_out1, demultiplexer_1_out2,
       demultiplexer_1_out3, demultiplexer_2_out0, demultiplexer_2_out1, demultiplexer_2_out2,
       demultiplexer_2_out3;
  wire [31:0] _0_data_out, _1_data_out, _2_data_out, _3_data_out;

  cache_entry _3 (
    .tag(addr[7:4]), .byte_offset(addr[1:0]), .data_in(data_in), .memRead(demultiplexer_2_out3),
    .memWrite(demultiplexer_1_out3), .clock(clock), .reset(reset), .miss(_3_miss), .data_out(_3_data_out));
  cache_entry _2 (
    .tag(addr[7:4]), .byte_offset(addr[1:0]), .data_in(data_in), .memRead(demultiplexer_2_out2),
    .memWrite(demultiplexer_1_out2), .clock(clock), .reset(reset), .miss(_2_miss), .data_out(_2_data_out));
  cache_entry _1 (
    .tag(addr[7:4]), .byte_offset(addr[1:0]), .data_in(data_in), .memRead(demultiplexer_2_out1),
    .memWrite(demultiplexer_1_out1), .clock(clock), .reset(reset), .miss(_1_miss), .data_out(_1_data_out));
  cache_entry _0 (
    .tag(addr[7:4]), .byte_offset(addr[1:0]), .data_in(data_in), .memRead(demultiplexer_2_out0),
    .memWrite(demultiplexer_1_out0), .clock(clock), .reset(reset), .miss(_0_miss), .data_out(_0_data_out));
  Demultiplexer #(.select(2)) demultiplexer_1 (
    .out0(demultiplexer_1_out0), .out1(demultiplexer_1_out1), .out2(demultiplexer_1_out2),
    .out3(demultiplexer_1_out3), .in(memWrite), .sel(addr[3:2]));  // open: en
  Demultiplexer #(.select(2)) demultiplexer_2 (
    .out0(demultiplexer_2_out0), .out1(demultiplexer_2_out1), .out2(demultiplexer_2_out2),
    .out3(demultiplexer_2_out3), .in(memRead), .sel(addr[3:2]));  // open: en
  Multiplexer #(.select(2)) multiplexer_1 (
    .in0(_0_miss), .in1(_1_miss), .in2(_2_miss), .in3(_3_miss), .out(miss), .sel(addr[3:2]));  // open: en
  Multiplexer #(.select(2), .width(32)) multiplexer_2 (
    .in0(_0_data_out), .in1(_1_data_out), .in2(_2_data_out), .in3(_3_data_out), .out(data_out),
    .sel(addr[3:2]));  // open: en

  // Other names for the same wires on the sheet: offsetT[1:0] = addr[1:0]; indexT[1:0] = addr[3:2];
  //   tagT[3:0] = addr[7:4]; data_inT[31:0] = data_in; enableT = memWrite

  // Notes on the sheet:
  //   Entradas e sinal de controle
endmodule

// entry
module cache_entry (
  input  memRead,
  input  [3:0] tag,
  input  [1:0] byte_offset,
  input  memWrite,
  input  [31:0] data_in,
  input  reset,
  input  clock,
  output miss,
  output [31:0] data_out
);

  wire and_1_out, comparator_1_eq, demultiplexer_1_out0, demultiplexer_1_out1, demultiplexer_1_out2,
       demultiplexer_1_out3, enableT, nand_1_out, validR_q;
  wire [3:0] tagR_q;
  wire [31:0] register_1_q, register_2_q, register_3_q, register_4_q;

  or or_1 (enableT, miss, memWrite);
  Demultiplexer #(.select(2)) demultiplexer_1 (
    .out0(demultiplexer_1_out0), .out1(demultiplexer_1_out1), .out2(demultiplexer_1_out2),
    .out3(demultiplexer_1_out3), .in(enableT), .sel(byte_offset));  // open: en
  Register #(.width(1)) validR (.D(enableT), .en(enableT), .Q(validR_q), .clk(clock), .clr(and_1_out));
  Register #(.width(4)) tagR (.D(tag), .en(enableT), .Q(tagR_q), .clk(clock), .clr(and_1_out));
  Register #(.width(32)) register_1 (
    .D(data_in), .en(demultiplexer_1_out0), .Q(register_1_q), .clk(clock), .clr(and_1_out));
  Register #(.width(32)) register_2 (
    .D(data_in), .en(demultiplexer_1_out1), .Q(register_2_q), .clk(clock), .clr(and_1_out));
  Register #(.width(32)) register_3 (
    .D(data_in), .en(demultiplexer_1_out2), .Q(register_3_q), .clk(clock), .clr(and_1_out));
  Register #(.width(32)) register_4 (
    .D(data_in), .en(demultiplexer_1_out3), .Q(register_4_q), .clk(clock), .clr(and_1_out));
  Multiplexer #(.select(2), .width(32)) multiplexer_1 (
    .in0(register_1_q), .in1(register_2_q), .in2(register_3_q), .in3(register_4_q), .out(data_out),
    .sel(byte_offset));  // open: en
  and and_1 (and_1_out, clock, reset);
  Comparator #(.width(4)) comparator_1 (.a(tagR_q), .b(tag), .eq(comparator_1_eq));  // open: gt, lt
  nand nand_1 (nand_1_out, validR_q, comparator_1_eq);
  and and_2 (miss, memRead, nand_1_out);

  // Other names for the same wires on the sheet: missT = miss; offsetT[1:0] = byte_offset; tagT[3:0] = tag
endmodule
